# Fritzing sketch ASK modules setup (saved by Fritzing 0.9.3b)

parts:
  Part1 = Arduino Uno (Rev3)
  JP1 = Header 4 [package=screwterminal-3.5mm-4_lock]
  JP2 = Header 4 [package=screwterminal-3.5mm-4_lock]

nets:
  N1: Part1.D11_PWM/MOSI, JP1.2
  N2: Part1.D12/MISO, JP2.2
  N3: Part1.GND, JP1.1, JP2.1
  N4: Part1.5V, JP1.4, JP2.3

notes:
  This is the IC1402
  comms rx module.
  Pins are gnd, rx, rx, vcc
  This is the IC1402
  comms TX module.
  Pins are gnd, tx, vcc
