# Fritzing sketch arducam mini 2MP wiring (saved by Fritzing 0.9.3b)
breadboards: 1

parts:
  Part1 = Arduino Uno (Rev3) - ICSP
  arducam1 = Arducam 5mp mini

nets:
  N1: Part1.A4/SDA, arducam1.SDA
  N2: Part1.A5/SCL, arducam1.SCL
  N3: Part1.ICSP_MISO, Part1.D12/MISO, arducam1.MOSI
  N4: Part1.D11_PWM/MOSI, arducam1.MISO
  N5: Part1.D13/SCK, arducam1.SCK
  N6: Part1.D7, arducam1.CS
  5V: Part1.5V, arducam1.VCC
  GND: Part1.GND, arducam1.GND

custom parts:
  Arducam 5mp mini: arducam mini is a 5mp camera with a i2c and spi interface
