# Fritzing sketch arducam mini sd card wiring (saved by Fritzing 0.9.3b)
breadboards: 1

parts:
  Part1 = Arduino Uno (Rev3) - ICSP
  arducam1 = Arducam 5mp mini
  Part2 = Adafruit MicroSD card breakout board [part_number="Adafruit #254"]

nets:
  N1: Part1.A4/SDA, arducam1.SDA
  N2: Part1.A5/SCL, arducam1.SCL
  N3: Part1.ICSP_MISO, Part1.D12/MISO, arducam1.MOSI, Part2.DO
  N4: Part1.D11_PWM/MOSI, arducam1.MISO, Part2.DI
  N5: Part1.D13/SCK, arducam1.SCK, Part2.CLK
  N6: Part1.D6_PWM, Part2.CS
  N7: Part1.D7, arducam1.CS
  VCC: Part1.5V, arducam1.VCC, Part2.VCC
  GND: Part1.GND, arducam1.GND, Part2.GND

custom parts:
  Arducam 5mp mini: arducam mini is a 5mp camera with a i2c and spi interface
  Adafruit MicroSD card breakout board: Not just a simple breakout board, this microSD adapter goes the extra mile - designed for ease of use. Onboard 5v->3v regulator provides 150mA for power-hungry cards 3v level shifting means you can use this with ease on either 3v or 5v systems Uses a proper level shifting chip, not resistors: less problems, and faster read/write access Use 3 or 4 digital pins to read and write 2Gb+ of storage!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
