# Fritzing sketch adafruit sd card basic test (saved by Fritzing 0.9.3b)
breadboards: 1

parts:
  Part1 = Arduino Uno (Rev3)
  Part2 = Adafruit MicroSD card breakout board [part_number="Adafruit #254"]

nets:
  N1: Part1.D11_PWM/MOSI, Part2.DI
  N2: Part1.D12/MISO, Part2.DO
  N3: Part1.D13/SCK, Part2.CLK
  N4: Part1.D6_PWM, Part2.CD
  5V: Part1.5V, Part2.VCC
  GND: Part1.GND, Part2.GND

custom parts:
  Adafruit MicroSD card breakout board: Not just a simple breakout board, this microSD adapter goes the extra mile - designed for ease of use. Onboard 5v->3v regulator provides 150mA for power-hungry cards 3v level shifting means you can use this with ease on either 3v or 5v systems Uses a proper level shifting chip, not resistors: less problems, and faster read/write access Use 3 or 4 digital pins to read and write 2Gb+ of storage!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
