# Fritzing sketch prototype arduino arducam (saved by Fritzing 0.9.3b)
breadboards: 1

parts:
  arducam1 = Arducam 5mp mini
  Part1 = Arduino Uno (Rev3)

nets:
  N1: arducam1.CS, Part1.D10_PWM/SS
  GND: arducam1.GND, Part1.GND
  VCC: arducam1.VCC, Part1.5V
  N2: arducam1.SDA, Part1.A4/SDA
  N3: arducam1.SCL, Part1.A5/SCL

custom parts:
  Arducam 5mp mini: arducam mini is a 5mp camera with a i2c and spi interface
